# Fritzing sketch weather_controller (saved by Fritzing 0.9.2b)
breadboards: 1

parts:
  C_H_I_P_1 = Next Thing Co. C.H.I.P
  R1 = Resistor [tolerance=±5% resistance=220 package="2512 [SMD]"]
  R2 = Resistor [tolerance=±5% resistance=220 package="2512 [SMD]"]
  Part1 = Adafruit Pro Trinket 5V 16MHz [part_number="Adafruit #2000"]
  J1 = RJ11 Jack [package=rj11-6]
  J2 = RJ11 Jack [package=rj11-6]
  R3 = Resistor [tolerance=±5% resistance=220 package=THT]

nets:
  GND: C_H_I_P_1.GND, Part1.GND, J1.6
  N1: C_H_I_P_1.CHG-IN, R1.Pin_0, R2.Pin_1, Part1.VBAT, J1.5, J2.3, J2.5, R3.Pin_1
  N2: C_H_I_P_1.CSIPCK, R1.Pin_1, J1.1
  N3: C_H_I_P_1.CSICK, R2.Pin_0, J1.2
  N4: J2.2, R3.Pin_0

notes:
  rJ-11 to weather vane
  RJ-11 to temp/humidity
  100K ohms x 2 for I2C
  4.7K ohm

custom parts:
  Adafruit Pro Trinket 5V 16MHz: Trinket's got a big sister in town - the Pro Trinket 5V! Pro Trinket combines everything you love about Trinket with the familiarity of the common core Arduino chip, the ATmega328. It's like an Arduino Pro Mini with more pins and USB tossed in, so delicious. Trinket's a year old now, and while its been great to see tons of tiny projects, sometimes you just need more pins, more FLASH, and more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
